# Fritzing sketch schem1 (saved by Fritzing 0.9.3b)
breadboards: 1

parts:
  R1 = Resistor [tolerance=±5% resistance=150 package=THT]
  LED1 = LED - 5mm [color="Red (633nm)" package="5 mm [THT]"]
  V1 = DC Power [voltage=3V]

nets:
  N1: R1.Pin_0, V1.V+
  N2: R1.Pin_1, LED1.anode
  N3: LED1.cathode, V1.V-
