# Fritzing sketch schem2 (saved by Fritzing 0.9.3b)
breadboards: 1

parts:
  V1 = DC Power [voltage=3V]
  R1 = Resistor [tolerance=±5% resistance=220 package=THT]
  R2 = Resistor [tolerance=±5% resistance=220 package=THT]
  ? = Resistor [tolerance=±5% resistance=220 package=THT]
  LED1 = LED - 5mm [color="Red (633nm)" package="5 mm [THT]"]
  LED2 = LED - 5mm [color="Red (633nm)" package="5 mm [THT]"]
  LED3 = LED - 5mm [color="Red (633nm)" package="5 mm [THT]"]

nets:
  N1: V1.V+, R1.Pin_0, R2.Pin_1, ?.Pin_1
  N2: V1.V-, LED1.cathode, LED2.cathode, LED3.cathode
  N3: R1.Pin_1, LED3.anode
  N4: R2.Pin_0, LED2.anode
  N5: ?.Pin_0, LED1.anode
