# Fritzing sketch dc+tip120 (saved by Fritzing 0.9.3b)

parts:
  Part1 = Adafruit Feather 32u4 Basic Proto [part_number="Adafruit #2771"]
  M1 = DC Motor
  Q1 = pnp-Powertransistor [part_number=TIP120 package="TO220 [THT]"]
  D1 = Rectifier Diode [part_number=1N4001 package="300 mil [THT]"]
  R1 = Resistor [tolerance=±5% resistance=2.2k package=THT]

nets:
  N1: Part1.GND, Q1.emitter
  N2: Part1.13, R1.Pin_0
  N3: M1.pin_1, Q1.collector, D1.anode
  N4: M1.pin_2, D1.cathode
  N5: Q1.base, R1.Pin_1

notes:
  GND - PSU
  Vcc - PSU

custom parts:
  Adafruit Feather 32u4 Basic Proto: At the Feather 32u4's heart is at ATmega32u4 clocked at 8 MHz and at 3.3V logic, a chip setup we've had tons of experience with as it's the same as the Flora. This chip has 32K of flash and 2K of RAM, with built in USB so not only does it have a USB-to-Serial program & debug capability built in with no need for an FTDI-like chip, it can also act like a mouse, keyboard, USB MIDI device, etc.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
