# Fritzing sketch SimpleL293D (saved by Fritzing 0.9.3b)
breadboards: 1

parts:
  IC1 = L293D [package=THT]
  M1 = DC Motor

nets:
  PWM/Voltage Control: IC1.Enable_1
  5V: IC1.In_1, IC1.+V
  N1: IC1.Out_1_(_Controlled_by_Enable_1_), M1.pin_1
  GND: IC1.0V
  N2: IC1.Out_2_(_Controlled_by_Enable_1_), M1.pin_2
  12V: IC1.+Vmotor
