// Logisim project wk2LogicCircuits.circ as structural Verilog: 5 circuits, main circuit NAND1
module NAND1 (
  input  in_1,
  input  in_2,
  output out_3
);

  wire and_1_out;

  and and_1 (and_1_out, in_1, in_2);
  not not_1 (out_3, and_1_out);
endmodule

module NAND2 (
  input  in_1,
  input  in_2,
  output out_3
);

  nand nand_1 (out_3, in_1, in_2);
endmodule

module NOR__INVAND (
  input  in_1,
  input  in_2,
  output out_3
);

  wire not_1_out, not_2_out;

  not not_1 (not_1_out, in_1);
  not not_2 (not_2_out, in_2);
  and and_1 (out_3, not_1_out, not_2_out);
endmodule

module AND__NAND (
  input  in_1,
  input  in_2,
  output out_3
);

  wire nand_1_out;

  nand nand_1 (nand_1_out, in_1, in_2);
  nand nand_2 (out_3, nand_1_out, nand_1_out);
endmodule

module OR__NAND (
  input  in_1,
  input  in_2,
  output out_3
);

  wire nand_1_out, nand_2_out;

  nand nand_1 (nand_1_out, in_1, in_1);
  nand nand_2 (nand_2_out, in_2, in_2);
  nand nand_3 (out_3, nand_1_out, nand_2_out);
endmodule
