# Fritzing sketch AM2320-SparkfunProRF (saved by Fritzing 0.9.3b)
breadboards: 1

parts:
  AM1 = AM2320 Humidity and Temperature Sensor [part_number="Adafruit #3721"]
  R1 = Resistor [tolerance=±5% resistance=10k package=THT]
  R2 = Resistor [tolerance=±5% resistance=10k package=THT]

nets (from the schematic view):
  3.3V: AM1.VDD, R1.Pin_0, R2.Pin_0
  D4: AM1.SDA, R1.Pin_1
  GND: AM1.GND
  D3: AM1.SCL, R2.Pin_1

notes:
  D3
  D4
  3.3V
  GND

custom parts:
  AM2320 Humidity and Temperature Sensor: AM2320 I2C Humidity and Temperature Sensor
