# Fritzing sketch SuperPositionEx1 (saved by Fritzing 0.9.2b)
breadboards: 1

parts:
  30Ω = Resistor [tolerance=±5% resistance=220 package=THT]
  15Ω = Resistor [tolerance=±5% resistance=220 package=THT]
  10Ω = Resistor [tolerance=±5% resistance=220 package=THT]
  V1 = DC Power [voltage=12V]
  V2 = DC Power [voltage=9V]
  V4 = DC Power [voltage=9V]
  7_5Ω = Resistor [tolerance=±5% resistance=220 package=THT]
  15Ω_2 = Resistor [tolerance=±5% resistance=220 package=THT]
  6Ω = Resistor [tolerance=±5% resistance=220 package=THT]
  30Ω_2 = Resistor [tolerance=±5% resistance=220 package=THT]
  V5 = DC Power [voltage=12V]

nets:
  N1: 30Ω.Pin_0, V1.V+
  N2: 30Ω.Pin_1, 15Ω.Pin_0, 10Ω.Pin_0
  N3: 15Ω.Pin_1, V2.V+
  GND: 10Ω.Pin_1, V1.V-, V2.V-
  N4: V4.V+, 15Ω_2.Pin_1
  N5: V4.V-, 7_5Ω.Pin_1
  N6: 7_5Ω.Pin_0, 15Ω_2.Pin_0
  N7: 6Ω.Pin_0, 30Ω_2.Pin_1
  N8: 6Ω.Pin_1, V5.V-
  N9: 30Ω_2.Pin_0, V5.V+
