# Fritzing sketch WheatstoneBridge (saved by Fritzing 0.9.2b)
breadboards: 1

parts:
  R1 = Rotary Potentiometer (Small) [maximum_resistance=10kΩ package=THT]
  ? = Resistor [tolerance=±5% resistance=220 package=THT]
  R1_2 = Resistor [tolerance=±5% resistance=330 package=THT]
  R4 = Resistor [tolerance=±5% resistance=4.7k package=THT]

nets:
  GND: R1.leg1, R1.wiper, ?.Pin_1
  V Test: R1.leg2, ?.Pin_0, R1_2.Pin_0, R4.Pin_1
  3.3V: R1_2.Pin_1, R4.Pin_0
