// Logisim project 4-1MUX_logic.circ as structural Verilog: 1 circuit, main circuit main
module main (
  input  a,
  input  b,
  input  W,
  input  X,
  input  Y,
  input  Z
);

  wire and_1_out, and_2_out, and_3_out, and_4_out, not_1_out, not_2_out, or_1_out;

  not not_1 (not_1_out, a);
  not not_2 (not_2_out, b);
  and and_1 (and_1_out, not_2_out, not_1_out, W);
  and and_2 (and_2_out, not_2_out, a, X);
  and and_3 (and_3_out, not_1_out, b, Y);
  and and_4 (and_4_out, a, b, Z);
  or or_1 (or_1_out, and_1_out, and_2_out, and_3_out, and_4_out);
  LED Q (.in(or_1_out));
endmodule
