// Logisim project 4-1MUX_logicNAND.circ as structural Verilog: 1 circuit, main circuit main
module main (
  input  W,
  input  X,
  input  Y,
  input  Z,
  input  b,
  input  a
);

  wire nand_1_out, nand_2_out, nand_3_out, nand_4_out, nand_5_out, nand_6_out, nand_7_out;

  nand nand_1 (nand_1_out, b, b);
  nand nand_2 (nand_2_out, a, a);
  nand nand_3 (nand_3_out, W, nand_1_out, nand_2_out);
  nand nand_4 (nand_4_out, X, a, nand_1_out);
  nand nand_5 (nand_5_out, Y, nand_2_out, b);
  nand nand_6 (nand_6_out, Z, a, b);
  nand nand_7 (nand_7_out, nand_3_out, nand_4_out, nand_5_out, nand_6_out);
  LED Q (.in(nand_7_out));
endmodule
