# Fritzing sketch Input.MotorSTM32 (saved by Fritzing 0.9.3b)
breadboards: 1

parts:
  J1 = STM32 Nucleo boards
  R1 = Resistor [tolerance=±5% resistance=220 package=THT]
  LED1 = LED - 3mm [color="Orange (612nm)" package="3 mm [THT]"]
  S1 = Pushbutton [package="[THT]"]
  Q1 = Basic FET N-Channel [package="TO220 [THT]"]
  M1 = DC Motor

nets:
  N1: J1.D12/MISO, S1.Pin_3, S1.Pin_4
  N2: J1.D5_PWM, Q1.gate
  N3: J1.D7, LED1.anode
  N4: J1.5V, M1.pin_2
  N5: R1.Pin_0, S1.Pin_1, S1.Pin_2, Q1.drain
  N6: R1.Pin_1, LED1.cathode
  N7: Q1.source, M1.pin_1
