# Fritzing sketch Diode_Intro (saved by Fritzing 0.9.2b)
breadboards: 1

parts:
  R1 = Resistor [tolerance=±5% resistance=220 package=THT]
  D1 = Rectifier Diode [part_number=1N4001 package="300 mil [THT]"]
  C1 = Ceramic Capacitor [capacitance=1µF package="100 mil [THT, multilayer]"]

nets:
  N1: R1.Pin_0, D1.cathode, C1.1
  Func. Gen. -/GND: R1.Pin_1, C1.0
  Func. Gen. +: D1.anode
