# Fritzing sketch Full Wave (saved by Fritzing 0.9.2b)
breadboards: 1

parts:
  V1 = AC Power [voltage=12V frequency=60]
  D1 = Rectifier Diode [part_number=1N4001 package="300 mil [THT]"]
  D2 = Rectifier Diode [part_number=1N4001 package="300 mil [THT]"]
  D3 = Rectifier Diode [part_number=1N4001 package="300 mil [THT]"]
  D4 = Rectifier Diode [part_number=1N4001 package="300 mil [THT]"]
  C1 = Electrolytic Capacitor [capacitance=1mF package="100 mil [THT, electrolytic]"]
  U1 = Voltage Regulator - 5V [package="DPak [SMD]"]
  C2 = Electrolytic Capacitor [capacitance=1mF package="100 mil [THT, electrolytic]"]

nets:
  N1: V1.V+, D1.cathode, D3.anode
  N2: V1.V-, D2.cathode, D4.anode
  GND: D1.anode, D2.anode, C1.-, U1.GND, C2.-
  N3: D3.cathode, D4.cathode, U1.input_voltage, C2.+
  5v Out: C1.+, U1.output_voltage
