# Fritzing sketch DRV8825Stepper (saved by Fritzing 0.9.2b)

parts:
  Power_plug1 = Power plug
  C1 = Electrolytic Capacitor [capacitance=0.1mF package="100 mil [THT, electrolytic]"]
  M1 = Stepper Motor - Bipolar
  Part1 = Arduino Uno (Rev3)
  R1 = Resistor [tolerance=±5% resistance=10k package=THT]
  DRV_1 = DRV 8825 Stepper Motor Carrier, High Current [part_number="DRV 8825"]

nets:
  N1: Power_plug1.GND, C1.-, DRV_1.GROUND_ST/_MT
  N2: Power_plug1.VCC, C1.+, DRV_1.VOLTAGE_ST/_MT
  N3: M1.A, DRV_1.OUT_1A
  N4: M1.C, DRV_1.OUT_2A
  N5: M1.B, DRV_1.OUT_1B
  N6: M1.D, DRV_1.OUT_2B
  N7: Part1.D8, R1.Pin_1, DRV_1.ENABLE
  N8: Part1.GND, DRV_1.GROUND_LOG
  N9: Part1.D2, DRV_1.STEP
  N10: Part1.D5_PWM, DRV_1.DIRECTION
  N11: Part1.5V, R1.Pin_0, DRV_1.MS1, DRV_1.MS2, DRV_1.VOLTAGE_DD
  N12: DRV_1.RESET, DRV_1.SLEEP

notes:
  12V IN
  Connect 12V to VIN and GND on Arduino when untethered
  NEMA 17 Bipolar Stepper Motor
