# Fritzing sketch relayPCB (saved by Fritzing 0.9.3b)
circuit board: 3.40635cm x 2.08958cm
breadboards: 1

parts:
  J3 = female pin header, 2 pins [form="♀ (female)"]
  J2 = female pin header, 1 pin [form="♀ (female)"]
  J1 = female pin header, 3 pins [form="♀ (female)"]
  S1 = Pushbutton [package=THT]
  J4 = female pin header, 1 pin [form="♀ (female)"]
  J5 = female pin header, 1 pin [form="♀ (female)"]

nets:
  N1: J3.pin1, J4.pin1
  N2: J3.pin2, S1.leg1
  N3: J2.pin1, J1.pin3
  N4: S1.leg0, J5.pin1

notes:
  COM
  NC
  NO
  ARM
  5V IN
  SWITCH
  E.M.
