# Fritzing sketch dc+tmp36 (saved by Fritzing 0.9.3b)

parts:
  Part1 = Adafruit Feather 32u4 Basic Proto [part_number="Adafruit #2771"]
  M1 = DC Motor
  D1 = Rectifier Diode [part_number=1N4001 package="300 mil [THT]"]
  R1 = Resistor [tolerance=±5% resistance=2.2k package=THT]
  TIP120 = npn-Powertransistor [package="TO220 [THT]"]
  TMP36 = TMP36 Temperature Sensor [package="TO92 [THT]"]
  R2 = Resistor [tolerance=±5% resistance=220 package=THT]
  R3 = Resistor [tolerance=±5% resistance=220 package=THT]
  LED1 = LED - 5mm [color="Red (633nm)" package="5 mm [THT]"]
  LED2 = LED - 5mm [color="Green (560nm)" package="5 mm [THT]"]
  PushButton = Pushbutton [package="[THT]"]
  R4 = Resistor [tolerance=±5% resistance=10k package=THT]

nets:
  GND: Part1.GND, TIP120.emitter, TMP36.GND, LED1.cathode, LED2.cathode, R4.Pin_0
  N1: Part1.A1, PushButton.Pin_1, PushButton.Pin_2, R4.Pin_1
  N2: Part1.A0, TMP36.Vout
  N3: Part1.+3V3, TMP36.+Vs, PushButton.Pin_3
  N4: Part1.13, R1.Pin_0
  N5: Part1.3, R2.Pin_0
  N6: Part1.2, R3.Pin_0
  N7: M1.pin_1, D1.anode, TIP120.collector
  N8: M1.pin_2, D1.cathode
  N9: R1.Pin_1, TIP120.base
  N10: R2.Pin_1, LED2.anode
  N11: R3.Pin_1, LED1.anode

notes:
  GND - PSU
  Vcc - PSU

custom parts:
  Adafruit Feather 32u4 Basic Proto: At the Feather 32u4's heart is at ATmega32u4 clocked at 8 MHz and at 3.3V logic, a chip setup we've had tons of experience with as it's the same as the Flora. This chip has 32K of flash and 2K of RAM, with built in USB so not only does it have a USB-to-Serial program & debug capability built in with no need for an FTDI-like chip, it can also act like a mouse, keyboard, USB MIDI device, etc.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
