# Fritzing sketch DC-L293D (saved by Fritzing 0.9.3b)

parts:
  Part1 = Adafruit Feather 32u4 Basic Proto [part_number="Adafruit #2771"]
  IC1 = L293D [package=THT]
  M1 = DC Motor

nets:
  N1: Part1.GND, IC1.0V
  N2: Part1.+3V3, IC1.+V
  N3: Part1.11, IC1.Enable_1
  N4: Part1.10, IC1.In_1
  N5: Part1.9, IC1.In_2
  N6: IC1.Out_1_(_Controlled_by_Enable_1_), M1.pin_2
  N7: IC1.Out_2_(_Controlled_by_Enable_1_), M1.pin_1

notes:
  V+ Motor
  GND Chip --> GND of Motor Voltage

custom parts:
  Adafruit Feather 32u4 Basic Proto: At the Feather 32u4's heart is at ATmega32u4 clocked at 8 MHz and at 3.3V logic, a chip setup we've had tons of experience with as it's the same as the Flora. This chip has 32K of flash and 2K of RAM, with built in USB so not only does it have a USB-to-Serial program & debug capability built in with no need for an FTDI-like chip, it can also act like a mouse, keyboard, USB MIDI device, etc.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
