# Fritzing sketch 1 Knob Servo Challenge (saved by Fritzing 0.9.3b)

parts:
  Part1 = Adafruit Feather 32u4 Basic Proto [part_number="Adafruit #2771"]
  R2 = Rotary Potentiometer (Small) [maximum_resistance=100kΩ package=THT]
  M2 = Dagu DGServo 9g (Top view) [part_number=RS001B]

nets:
  N1: Part1.A0, R2.wiper
  N2: Part1.GND, R2.leg2
  N3: Part1.+3V3, R2.leg1
  N4: Part1.9, M2.pulse

notes:
  PSU +
  GND PSU

custom parts:
  Adafruit Feather 32u4 Basic Proto: At the Feather 32u4's heart is at ATmega32u4 clocked at 8 MHz and at 3.3V logic, a chip setup we've had tons of experience with as it's the same as the Flora. This chip has 32K of flash and 2K of RAM, with built in USB so not only does it have a USB-to-Serial program & debug capability built in with no need for an FTDI-like chip, it can also act like a mouse, keyboard, USB MIDI device, etc.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
