# Fritzing sketch 2 Servo Challenge (saved by Fritzing 0.9.3b)

parts:
  Part1 = Adafruit Feather 32u4 Basic Proto [part_number="Adafruit #2771"]
  R1 = Resistor [tolerance=±5% resistance=220 package=THT]
  LED1 = LED - 5mm [color="Red (633nm)" package="5 mm [THT]"]
  R2 = Rotary Potentiometer (Small) [maximum_resistance=100kΩ package=THT]
  R3 = Rotary Potentiometer (Small) [maximum_resistance=100kΩ package=THT]
  S1 = Pushbutton [package="[THT]"]
  R4 = Resistor [tolerance=±5% resistance=10k package=THT]
  M1 = Dagu DGServo 9g (Top view) [part_number=RS001B]
  M2 = Dagu DGServo 9g (Top view) [part_number=RS001B]
  S2 = Pushbutton [package="[THT]"]
  R5 = Resistor [tolerance=±5% resistance=10k package=THT]

nets:
  N1: Part1.GND, LED1.cathode, R2.leg2, R3.leg2, R4.Pin_0, R5.Pin_0
  N2: Part1.A1, R3.wiper
  N3: Part1.A0, R2.wiper
  N4: Part1.+3V3, R2.leg1, R3.leg1, S1.Pin_1, S1.Pin_2, S2.Pin_1, S2.Pin_2
  N5: Part1.12, R1.Pin_1
  N6: Part1.10, M1.pulse
  N7: Part1.9, M2.pulse
  N8: Part1.3, S2.Pin_3, S2.Pin_4, R5.Pin_1
  N9: Part1.2, S1.Pin_3, S1.Pin_4, R4.Pin_1
  N10: R1.Pin_0, LED1.anode

notes:
  PSU +
  GND PSU

custom parts:
  Adafruit Feather 32u4 Basic Proto: At the Feather 32u4's heart is at ATmega32u4 clocked at 8 MHz and at 3.3V logic, a chip setup we've had tons of experience with as it's the same as the Flora. This chip has 32K of flash and 2K of RAM, with built in USB so not only does it have a USB-to-Serial program & debug capability built in with no need for an FTDI-like chip, it can also act like a mouse, keyboard, USB MIDI device, etc.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
