# Fritzing sketch SimpleTIP120 (saved by Fritzing 0.9.3b)
breadboards: 1

parts:
  Q1 = npn-Powertransistor [package="TO220 [THT]"]
  R1 = Resistor [tolerance=±5% resistance=1k package=THT]
  M1 = DC Motor
  D1 = Rectifier Diode [part_number=1N4001 package="300 mil [THT]"]

nets:
  N1: Q1.base, R1.Pin_1
  N2: Q1.collector, M1.pin_1, D1.anode
  GND: Q1.emitter
  PWM/Voltage Input: R1.Pin_0
  12V: M1.pin_2, D1.cathode
