// Logisim project 2-1MUX_logic.circ as structural Verilog: 1 circuit, main circuit main
module main (
  input  X,
  input  A,
  input  Y
);

  wire nand_1_out, nand_2_out, nand_3_out, nand_4_out;

  nand nand_1 (nand_1_out, A, A);
  nand nand_2 (nand_2_out, X, A);
  nand nand_3 (nand_3_out, nand_1_out, Y);
  nand nand_4 (nand_4_out, nand_2_out, nand_3_out);
  LED Q (.in(nand_4_out));
endmodule
