# Fritzing sketch FullWave+Filter+7805 (saved by Fritzing 0.9.2b)
breadboards: 1

parts:
  D1 = Rectifier Diode [part_number=1N4001 package="300 mil [THT]"]
  D2 = Rectifier Diode [part_number=1N4001 package="300 mil [THT]"]
  D3 = Rectifier Diode [part_number=1N4001 package="300 mil [THT]"]
  D4 = Rectifier Diode [part_number=1N4001 package="300 mil [THT]"]
  V1 = AC Power [voltage=12V frequency=60]
  U1 = Voltage Regulator - 5V [part_number=7805 package="TO220 [THT]"]
  1000µF = Electrolytic Capacitor [capacitance=100µF voltage=50V package="300 mil [THT, electrolytic]"]
  1000µF1 = Electrolytic Capacitor [capacitance=100µF voltage=50V package="300 mil [THT, electrolytic]"]

nets:
  N1: D1.cathode, D3.anode, V1.V+
  GND/O-SCOPE GND: D1.anode, D2.anode, U1.GND, 1000µF.-, 1000µF1.-
  N2: D2.cathode, D4.anode, V1.V-
  N3: D3.cathode, D4.cathode, U1.input_voltage, 1000µF.+
  O-SCOPE: U1.output_voltage, 1000µF1.+
