# Fritzing sketch amp_lm308 (saved by Fritzing 0.9.3b)
breadboards: 1

parts:
  IC1 = IC, DIP package, 14 pins [chip_label=LM380]
  SP1 = SPEAKER [package=pcb_mount_speaker]
  R1 = Trimmer Potentiometer [maximum_resistance=10kΩ package=THT]
  C1 = Ceramic Capacitor [capacitance=0.1µF package="100 mil [THT, multilayer]"]
  C2 = Ceramic Capacitor [capacitance=100nF part_number=VALUE package="100 mil [THT, multilayer]"]
  C3 = Ceramic Capacitor [capacitance=0.1µF part_number=500µF package="100 mil [THT, multilayer]"]
  R2 = Resistor [tolerance=±5% resistance=470 package=THT]
  U1 = 2.5mm Audio Jack [package=stereojack2.5mm_specia_pogopins]

nets:
  N1: IC1.pin1, C2.1
  N2: IC1.pin6, R1.wiper
  GND: IC1.pin7, SP1.-, R1.leg1, C2.0, R2.Pin_1, U1.SLEEVE
  N3: IC1.pin8, C3.1
  9V: IC1.pin14
  N4: SP1.+, C3.0, R2.Pin_0
  N5: R1.leg2, C1.0
  N6: C1.1, U1.LEFT

notes:
  Pins 3, 4, 5, 10, 11, 12 to GND
