# Fritzing sketch ResistorLadder (saved by Fritzing 0.9.3b)
breadboards: 1

parts:
  S1 = Pushbutton [package=THT]
  S2 = Pushbutton [package=THT]
  S3 = Pushbutton [package=THT]
  S4 = Pushbutton [package=THT]
  R1 = Resistor [tolerance=±5% resistance=220 part_number=2*R package=THT]
  R2 = Resistor [tolerance=±5% resistance=220 part_number=R package=THT]
  R9 = Resistor [tolerance=±5% resistance=220 part_number=2*R package=THT]
  R10 = Resistor [tolerance=±5% resistance=220 part_number=R package=THT]
  R11 = Resistor [tolerance=±5% resistance=220 part_number=R package=THT]
  R12 = Resistor [tolerance=±5% resistance=220 part_number=2*R package=THT]
  R13 = Resistor [tolerance=±5% resistance=220 part_number=2*R package=THT]
  R14 = Resistor [tolerance=±5% resistance=220 part_number=2*R package=THT]

nets:
  N1: S1.leg0, R1.Pin_0
  5V: S1.leg1, S2.leg1, S3.leg1, S4.leg1
  N2: S2.leg0, R13.Pin_0
  N3: S3.leg0, R12.Pin_0
  N4: S4.leg0, R9.Pin_0
  Test Point: R1.Pin_1, R2.Pin_0
  N5: R2.Pin_1, R10.Pin_0, R13.Pin_1
  N6: R9.Pin_1, R11.Pin_1, R14.Pin_0
  N7: R10.Pin_1, R11.Pin_0, R12.Pin_1
  GND: R14.Pin_1
