# Fritzing sketch Simple_Lamp (saved by Fritzing 0.9.2b)
breadboards: 1

parts:
  R1 = Resistor [tolerance=±5% resistance=220 package=THT]
  LED1 = LED - 5mm [color="Red (633nm)" package="5 mm [THT]"]
  LED2 = LED - 5mm [color="Red (633nm)" package="5 mm [THT]"]
  R2 = Resistor [tolerance=±5% resistance=220 package=THT]
  R3 = Trimmer Potentiometer [maximum_resistance=10kΩ package=THT]
  R4 = Photocell (LDR) [package=THT]
  9V = Battery block 9V

nets:
  N1: R1.Pin_0, R2.Pin_0, 9V.+
  N2: R1.Pin_1, LED1.anode, R4.pin_0
  N3: LED1.cathode, LED2.cathode, R3.leg1, R3.wiper, R4.pin_1, 9V.-
  N4: LED2.anode, R2.Pin_1, R3.leg2
