# Fritzing sketch AND_Gate_Lab1 (saved by Fritzing 0.9.3b)
breadboards: 1

parts:
  IC1 = IC, DIP package, 14 pins [chip_label=7408]
  S1 = Pushbutton [package="[THT]"]
  S2 = Pushbutton [package="[THT]"]  # not connected
  LED1 = LED - 5mm [color="Red (633nm)" package="5 mm [THT]"]
  R1 = Resistor [tolerance=±5% resistance=220 package=THT]

nets:
  N1: IC1.pin3, R1.Pin_0
  5V: IC1.pin14
  N2: S1.Pin_1, S1.Pin_2
  GND: S1.Pin_3, S1.Pin_4, LED1.cathode
  N3: LED1.anode, R1.Pin_1

notes:
  5V
