# Fritzing sketch Temp.LightsSTM32 (saved by Fritzing 0.9.3b)
breadboards: 1

parts:
  J1 = STM32 Nucleo boards
  U1 = TMP36 [package=to-92-kit]
  LED1 = LED - 5mm [color="Red (633nm)" package="5 mm [THT]"]
  LED2 = LED - 5mm [color="Green (565nm)" package="5 mm [THT]"]
  LED3 = LED - 5mm [color="Orange (620nm)" package="5 mm [THT]"]

nets:
  N1: J1.A0, U1.VOUT
  GND: J1.GND, U1.GND, LED1.cathode, LED2.cathode, LED3.cathode
  N2: J1.D8, LED2.anode
  N3: J1.D6_PWM, LED1.anode
  N4: J1.D7, LED3.anode
  5V: J1.5V, U1.VCC
