# Fritzing sketch 5V Power Supply (saved by Fritzing 0.9.2b)
breadboards: 1

parts:
  D1 = Rectifier Diode [part_number=1N4001 package="300 mil [THT]"]
  D2 = Rectifier Diode [part_number=1N4001 package="300 mil [THT]"]
  D3 = Rectifier Diode [part_number=1N4001 package="300 mil [THT]"]
  D4 = Rectifier Diode [part_number=1N4001 package="300 mil [THT]"]
  U1 = Voltage Regulator - 5V [part_number=7805 package="TO220 [THT]"]
  1000µF = Electrolytic Capacitor [capacitance=100µF voltage=50V package="300 mil [THT, electrolytic]"]
  1000µF_2 = Electrolytic Capacitor [capacitance=100µF voltage=50V package="300 mil [THT, electrolytic]"]
  LED = LED - 5mm [color="Red (633nm)" package="5 mm [THT]"]
  TRANSFORMER = Transformer [package=transformer]
  120VAC = AC Power [voltage=5 frequency=60]
  R1 = Resistor [tolerance=±5% resistance=220 package=THT]
  SPST_AC = Pushbutton [package=THT]

nets:
  N1: D1.cathode, D3.anode, TRANSFORMER.4
  GND/GND OUT: D1.anode, D2.anode, U1.GND, 1000µF.-, 1000µF_2.-, LED.cathode
  N2: D2.cathode, D4.anode, TRANSFORMER.3
  N3: D3.cathode, D4.cathode, U1.input_voltage, 1000µF.+
  5V DC OUT: U1.output_voltage, 1000µF_2.+, R1.Pin_0
  N4: LED.anode, R1.Pin_1
  N5: TRANSFORMER.1, SPST_AC.leg1
  N6: TRANSFORMER.2, 120VAC.V-
  N7: 120VAC.V+, SPST_AC.leg0
